# Fritzing sketch button (saved by Fritzing 0.8.5b)
breadboards: 1

parts:
  Part1 = Arduino Leonardo (Rev3b)
  S1 = Momentary Switch [package=ksa_sealed_tac_switch]
  R1 = Resistor [tolerance=±5% resistance=220 package=THT]

nets:
  N1: Part1.D2/SDA, S1.1, R1.Pin_0
  N2: Part1.5V, S1.4
  N3: Part1.GND, R1.Pin_1
