# Fritzing sketch dial (saved by Fritzing 0.8.5b)
breadboards: 1

parts:
  Part1 = Arduino Leonardo (Rev3b)
  R1 = Rotary Potentiometer (Small) [maximum_resistance=100kΩ package=THT]

nets:
  N1: Part1.5V, R1.leg2
  N2: Part1.GND, R1.leg1
  N3: Part1.A2, R1.wiper
