# Fritzing sketch lights (saved by Fritzing 0.8.0b)
breadboards: 1

parts:
  Part1 = Arduino Leonardo (Rev3b)
  S1 = Pushbutton [package=THT]
  R1 = Resistor [tolerance=±5% resistance=220 package=THT]
  R2 = Resistor [tolerance=±5% resistance=220 package=THT]
  LED1 = LED - 5mm [color="Red (633nm)" package="5 mm [THT]"]

nets:
  N1: Part1.D5_PWM, S1.leg1, R1.Pin_1
  N2: Part1.5V, S1.leg0
  N3: Part1.GND, R1.Pin_0, R2.Pin_0
  N4: Part1.D13_PWM, LED1.anode
  N5: R2.Pin_1, LED1.cathode
